# Fritzing sketch M0Logger+LSM6DSOX (saved by Fritzing 0.9.5d)

parts:
  LSM6DSOX1 = Adafruit_LSM6DSOX
  Composant1 = Adafruit Feather M0 Adalogger [part_number="Adafruit #2796"]

nets:
  GND: LSM6DSOX1.GND, Composant1.GND
  3.3V: LSM6DSOX1.3.3V, Composant1.+3V3
  N1: LSM6DSOX1.SCL, Composant1.SCL
  N2: LSM6DSOX1.SDA, Composant1.SDA

custom parts:
  Adafruit Feather M0 Adalogger: This is the Adafruit Feather M0 Adalogger - our take on an 'all-in-one' Cortex M0 datalogger (or data-reader) with built in USB and battery charging. Its an Adafruit Feather M0 with a microSD holder ready to rock! We have other boards in the Feather family, check'em out here At the Feather M0's heart is an ATSAMD21G18 ARM Cortex M0 processor, clocked at 48 MHz and at 3.3V logic, the same one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
