# Fritzing sketch RX-WirelessTracker (saved by Fritzing 0.9.5d)

parts:
  Mod1 = Heltec Wireless Tracker
  microSD1 = MicroSD Card Module

nets:
  N1: Mod1.pin_1, microSD1.CS
  N2: Mod1.pin_4, microSD1.SCK
  N3: Mod1.pin_8, microSD1.MOSI
  N4: Mod1.pin_9, microSD1.MISO
  N5: Mod1.pin_26, microSD1.GND
  N6: Mod1.pin_27, microSD1.VCC

custom parts:
  Heltec Wireless Tracker: The Wireless Tracker card from Heltec.
