# Fritzing sketch TX-WirelessTracker-Apart (saved by Fritzing 0.9.5d)

parts:
  Mod1 = Heltec Wireless Tracker
  microSD1 = MicroSD Card Module
  Part1 = Adafruit Feather M0 Adalogger [part_number="Adafruit #2796"]
  Part2 = Adafruit Precision 9-DoF LSM6DSOX + LIS3MDL FeatherWing [part_number="Adafruit #4565"]
  LSM6DSOX1 = Adafruit_LSM6DSOX
  Part3 = Adafruit LSM6DSO32
  Part7 = Arduino Nano (Rev3.0)
  microSD3 = MicroSD Card Module
  Part8 = Barometric Pressure Sensor - BMP180 Breakout (GY-68)
  U2 = SLIDER [package=slider]

nets:
  N1: Mod1.pin_1, microSD1.CS
  N2: Mod1.pin_4, microSD1.SCK
  N3: Mod1.pin_8, microSD1.MOSI
  N4: Mod1.pin_9, microSD1.MISO
  N5: Mod1.pin_15, LSM6DSOX1.SDA
  N6: Mod1.pin_16, LSM6DSOX1.SCL
  GND: Mod1.pin_26, microSD1.GND, LSM6DSOX1.GND
  VCC: Mod1.pin_27, microSD1.VCC, LSM6DSOX1.VCC
  GND_2: Part1.GND, Part2.GND, Part3.GND
  +3V3: Part1.+3V3, Part2.3.3V, Part3.VCC
  N7: Part1.SCL, Part2.SCL, Part3.SCL
  N8: Part1.SDA, Part2.SDA, Part3.SDA
  N9: Part7.D10, microSD3.CS
  N10: Part7.D11/MOSI, microSD3.MOSI
  N11: Part7.D12/MISO, microSD3.MISO
  VCC_2: Part7.VIN, microSD3.VCC, Part8.VCC, U2.S
  GND_3: Part7.GND, microSD3.GND, Part8.GND, U2.A
  N12: Part7.A5, Part8.SCL
  N13: Part7.A4, Part8.SDA
  N14: Part7.A0, U2.E
  N15: Part7.D13/SCK, microSD3.SCK

custom parts:
  Heltec Wireless Tracker: The Wireless Tracker card from Heltec.
  Adafruit Feather M0 Adalogger: This is the Adafruit Feather M0 Adalogger - our take on an 'all-in-one' Cortex M0 datalogger (or data-reader) with built in USB and battery charging. Its an Adafruit Feather M0 with a microSD holder ready to rock! We have other boards in the Feather family, check'em out here At the Feather M0's heart is an ATSAMD21G18 ARM Cortex M0 processor, clocked at 48 MHz and at 3.3V logic, the same one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
  Adafruit Precision 9-DoF LSM6DSOX + LIS3MDL FeatherWing: Upgrade any Feather board with precision motion sensing with the ST 9-DoF IMU, an all-in-one sensing 'Wing. It sports two fantastic sensors from ST to provide 9 degrees of full-motion data. The board includes an LSM6DSOX, a 6-DoF IMU accelerometer + gyro. The 3-axis accelerometer can tell you which direction is down towards the Earth (by measuring gravity) or how fast the board is accelerating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
